# Fritzing sketch multitask_example1_setup (saved by Fritzing 0.8.5b)
circuit board: 8.46667cm x 5.64444cm
breadboards: 1

parts:
  Part1 = Arduino Uno (Rev3)
  VCC1 = Battery
  VCC2 = Battery
  J1 = Basic Servo
  J2 = Basic Servo

nets:
  N1: Part1.D9_PWM, J1.pulse
  N2: Part1.D10_PWM/SS, J2.pulse
  GND: Part1.GND, VCC2.-, J1.gnd, J2.gnd
  VCC: Part1.5V, J1.vcc, J2.vcc
  N3: Part1.VIN, VCC1.+
  N4: VCC1.-, VCC2.+
